# Fritzing sketch motor_diagram (saved by Fritzing 0.9.2b)
breadboards: 1

parts:
  Part1 = Arduino Due (Rev2b)  # not connected
  Part2 = Arduino XBee Shield
  IC1 = H-Bridge [package=THT]
  M1 = DC Motor
  BAT1 = BC9VPC [package=bc9vpc]  # not connected

nets:
  N1: Part2.5V, IC1.VCC1
  N2: Part2.D7, IC1.2A
  N3: Part2.D8, IC1.1A
  N4: Part2.D9, IC1.1_2EN
  GND: Part2.GND, IC1.GND3, IC1.GND4
  N5: IC1.1Y, M1.pin_2
  GND1: IC1.GND1, IC1.GND2
  N6: IC1.2Y, M1.pin_1

notes:
  Arduino Due with Xbee Shield
  H bridge to control a DC motor. This was used instead of a Motor sheild as use of an external motor library was not desirable.
